# Fritzing sketch Christmas Rickroll (saved by Fritzing 0.9.3b)
perfboards: 1

parts:
  Part1 = Arduino Uno (Rev3)
  microSD1 = MicroSD Card Module
  Part2 = Adafruit PAM8302 [part_number="Adafruit #2130"]
  C1 = Electrolytic Capacitor [capacitance=100μF package="0807 [SMD, electrolytic]"]
  C2 = Electrolytic Capacitor [capacitance=100μF package="0807 [SMD, electrolytic]"]
  OMRON1 = OMRON PCB Power Relay – G5LE [part_number="G5LE-1\r\n" package=THT]
  R1 = Resistor [tolerance=±20% resistance=220 package=THT]
  VCC1 = Battery
  S1 = Round Pushbutton
  SP1 = SPEAKER [package=pcb_mount_speaker]

nets:
  N1: Part1.D9_PWM, Part2.AIN+, C1.-, C2.-
  N2: Part1.D11_PWM/MOSI, microSD1.MOSI
  N3: Part1.D12/MISO, microSD1.MISO
  N4: Part1.D13/SCK, microSD1.SCK
  N5: Part1.GND, OMRON1.COIL1, S1.leg0
  N6: Part1.D2, S1.leg1
  N7: Part1.D3_PWM, OMRON1.COIL2
  N8: Part1.D4, microSD1.CS
  5V: Part1.5V, microSD1.VCC
  N9: Part2.VO+, SP1.-
  N10: Part2.VO-, SP1.+
  N11: C1.+, C2.+
  N12: OMRON1.C, VCC1.+
  N13: OMRON1.B, R1.Pin_1
  N14: R1.Pin_0, VCC1.-

notes:
  Ground
  5V
  Lamp

custom parts:
  Adafruit PAM8302: This super small mono amplifier is surprisingly powerful - able to deliver up to 2.5 Watts into 4-8 ohm impedance speakers. Inside the miniature chip is a class D controller, able to run from 2.0V-5.5VDC. Since the amp is a class D, its very efficient (over 90% efficient when driving an 8Ω speaker at over half a Watt) - making it perfect for portable and battery-powered projects. It has built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
